// Logisim project Q1_rs_latch.circ as structural Verilog
module main (
  input  r,
  input  s,
  input  in_3,
  input  in_4,
  output q,
  output q_bar,
  output out_7,
  output out_8
);

  nor nor_1 (q, r, q_bar);
  nor nor_2 (q_bar, s, q);
  rs_latch rs_latch_1 (.s(in_3), .r(in_4), .q(out_7), .q_bar(out_8));
endmodule

// VHDL entity rs_latch, as the project stores it:
library ieee;
use ieee.std_logic_1164.all;

entity rs_latch is
    port (
        s, r : in std_logic;
        q, q_bar : out std_logic
    );
end rs_latch;

architecture gate_level of rs_latch is
    signal qi, qbi : std_logic;
begin
    qi  <= not (r or qbi);
    qbi <= not (s or qi);
    q <= qi;
    q_bar <= qbi;
end gate_level;
