// Logisim project Q2_d_latch.circ as structural Verilog
module main (
  input  D,
  input  en,
  input  in_3,
  input  in_4,
  output q_bar,
  output q,
  output out_7,
  output out_8
);

  wire nand_1_out, nand_2_out, nand_4_out;

  nand nand_1 (nand_1_out, D, D);
  nand nand_2 (nand_2_out, D, en);
  nand nand_3 (q, nand_2_out, q_bar);
  nand nand_4 (nand_4_out, nand_1_out, en);
  d_latch d_latch_1 (.d(in_3), .en(in_4), .q(out_7), .q_bar(out_8));
  nand nand_5 (q_bar, nand_4_out, q);

  // Notes on the sheet:
  //   D_bar
  //   S_bar
  //   Q
  //   R_bar
  //   Q_bar
endmodule

module gate_d_latch (
  input  D,
  input  en,
  output Q_bar,
  output Q
);

  wire nand_1_out, nand_2_out, nand_3_out;

  nand nand_1 (nand_1_out, D, D);
  nand nand_2 (nand_2_out, D, en);
  nand nand_3 (nand_3_out, nand_1_out, en);
  nand nand_4 (Q, nand_2_out, Q_bar);
  nand nand_5 (Q_bar, nand_3_out, Q);

  // Notes on the sheet:
  //   D_bar
  //   S_bar
  //   R_bar
  //   Q
  //   Q_bar
endmodule

// VHDL entity d_latch, as the project stores it:
library ieee;
use ieee.std_logic_1164.all;

entity d_latch is
    port (
        d, en : in std_logic;
        q, q_bar : out std_logic
    );
end d_latch;

architecture rtl of d_latch is
    signal qi : std_logic;
begin
    process(d, en)
    begin
        if en = '1' then
            qi <= d;
        end if;
    end process;

    q <= qi;
    q_bar <= not qi;
end rtl;
