// Logisim project Q3_d_ff.circ as structural Verilog
module main (
  input  D,
  input  clk,
  input  in_3,
  input  in_4,
  output q_bar,
  output q,
  output out_7,
  output out_8
);

  wire nand_1_out, nand_2_out, nand_3_out, nand_4_out, nand_5_out, nand_6_out, nand_7_out, nand_9_out,
       not_1_out;

  not not_1 (not_1_out, clk);
  nand nand_1 (nand_1_out, D, D);
  nand nand_2 (nand_2_out, D, not_1_out);
  nand nand_3 (nand_3_out, nand_6_out, nand_6_out);
  nand nand_4 (nand_4_out, nand_6_out, clk);
  nand nand_5 (nand_5_out, nand_1_out, not_1_out);
  nand nand_6 (nand_6_out, nand_2_out, nand_9_out);
  nand nand_7 (nand_7_out, nand_3_out, clk);
  nand nand_8 (q, nand_4_out, q_bar);
  d_ff d_ff_1 (.d(in_3), .clk(in_4), .q(out_7), .q_bar(out_8));
  nand nand_9 (nand_9_out, nand_5_out, nand_6_out);
  nand nand_10 (q_bar, nand_7_out, q);

  // Notes on the sheet:
  //   D_bar
  //   S_bar
  //   D_bar
  //   S_bar
  //   Q
  //   Q
  //   R_bar
  //   R_bar
  //   Q_bar
  //   Q_bar
endmodule

module gate_d_latch (
  input  D,
  input  en
);

  wire nand_1_out, nand_2_out, nand_3_out, nand_4_out, nand_5_out;

  nand nand_1 (nand_1_out, D, D);
  nand nand_2 (nand_2_out, D, en);
  nand nand_3 (nand_3_out, nand_1_out, en);
  nand nand_4 (nand_4_out, nand_2_out, nand_5_out);
  nand nand_5 (nand_5_out, nand_3_out, nand_4_out);

  // Notes on the sheet:
  //   D_bar
  //   S_bar
  //   R_bar
  //   Q
  //   Q_bar
endmodule

// VHDL entity d_ff, as the project stores it:
library ieee;
use ieee.std_logic_1164.all;

entity d_ff is
    port (
        d, clk : in std_logic;
        q, q_bar : out std_logic
    );
end d_ff;

architecture rtl of d_ff is
    signal qi : std_logic;
begin
    process(clk)
    begin
        if rising_edge(clk) then
            qi <= d;
        end if;
    end process;

    q <= qi;
    q_bar <= not qi;
end rtl;

// VHDL entity d_latch, as the project stores it:
library ieee;
use ieee.std_logic_1164.all;

entity d_latch is
    port (
        d, en : in std_logic;
        q, q_bar : out std_logic
    );
end d_latch;

architecture rtl of d_latch is
    signal qi : std_logic;
begin
    process(d, en)
    begin
        if en = '1' then
            qi <= d;
        end if;
    end process;

    q <= qi;
    q_bar <= not qi;
end rtl;
