// Logisim project Q4_jk_ff.circ as structural Verilog
module main (
  input  k,
  input  j,
  input  clk,
  input  in_4,
  input  in_5,
  input  in_6,
  output q_bar,
  output q,
  output out_9,
  output out_10
);

  wire nand_1_out, nand_2_out, nand_3_out, nand_4_out, nand_5_out, nand_6_out, nand_7_out, nand_8_out,
       nand_9_out, nand_10_out, nand_12_out, nand_13_out, nand_14_out;

  nand nand_1 (nand_1_out, k, k);
  nand nand_2 (nand_2_out, clk, clk);
  nand nand_3 (nand_3_out, nand_1_out, q);
  nand nand_4 (nand_4_out, j, q_bar);
  nand nand_5 (nand_5_out, nand_13_out, nand_13_out);
  nand nand_6 (nand_6_out, nand_13_out, clk);
  jk_ff jk_ff_1 (.j(in_4), .k(in_5), .clk(in_6), .q(out_9), .q_bar(out_10));
  nand nand_7 (nand_7_out, nand_3_out, nand_4_out);
  nand nand_8 (nand_8_out, nand_7_out, nand_7_out);
  nand nand_9 (nand_9_out, nand_7_out, nand_2_out);
  nand nand_10 (nand_10_out, nand_5_out, clk);
  nand nand_11 (q, nand_6_out, q_bar);
  nand nand_12 (nand_12_out, nand_8_out, nand_2_out);
  nand nand_13 (nand_13_out, nand_9_out, nand_14_out);
  nand nand_14 (nand_14_out, nand_12_out, nand_13_out);
  nand nand_15 (q_bar, nand_10_out, q);

  // Notes on the sheet:
  //   k_bar
  //   clk_bar
  //   q
  //   q_bar
  //   B
  //   A
  //   d_next
  //   Q
  //   clk_bar
  //   d_next
  //   D_bar
  //   S_bar
  //   D_bar
  //   S_bar
  //   clk_bar
  //   R_bar
  //   q
  //   R_bar
  //   Q
  //   Q_bar
  //   q_bar
endmodule

module gate_d_latch (
  input  D,
  input  en,
  output q_bar,
  output q
);

  wire nand_1_out, nand_2_out, nand_3_out;

  nand nand_1 (nand_1_out, D, D);
  nand nand_2 (nand_2_out, D, en);
  nand nand_3 (nand_3_out, nand_1_out, en);
  nand nand_4 (q, nand_2_out, q_bar);
  nand nand_5 (q_bar, nand_3_out, q);

  // Notes on the sheet:
  //   D_bar
  //   S_bar
  //   Q
  //   R_bar
  //   Q_bar
endmodule

// VHDL entity jk_ff, as the project stores it:
library ieee;
use ieee.std_logic_1164.all;

entity jk_ff is
    port (
        j, k, clk : in std_logic;
        q, q_bar : out std_logic
    );
end jk_ff;

architecture rtl of jk_ff is
    signal qi : std_logic;
begin
    process(clk)
    begin
        if rising_edge(clk) then
            if j = '0' and k = '0' then
                null;
            elsif j = '0' and k = '1' then
                qi <= '0';
            elsif j = '1' and k = '0' then
                qi <= '1';
            elsif j = '1' and k = '1' then
                qi <= not qi;
            end if;
        end if;
    end process;

    q <= qi;
    q_bar <= not qi;
end rtl;
