// Logisim project Q5_d_ff_async.circ as structural Verilog
module main (
  input  clr,
  input  set,
  input  clk,
  input  d,
  input  in_5,
  input  in_6,
  input  in_7,
  input  in_8,
  output q,
  output q_bar,
  output out_11,
  output out_12
);

  wire and_1_out, and_2_out, and_3_out, and_4_out, and_5_out, and_6_out, nand_1_out, nand_2_out, nor_1_out,
       nor_2_out, nor_3_out, nor_4_out, not_1_out, not_2_out, not_3_out, not_4_out, not_5_out, not_6_out,
       not_7_out, or_1_out, or_2_out;

  not not_1 (not_1_out, clr);
  and and_1 (and_1_out, not_1_out, set);
  or or_1 (or_1_out, clr, set);
  not not_2 (not_2_out, clk);
  not not_3 (not_3_out, d);
  not not_4 (not_4_out, clr);
  not not_5 (not_5_out, or_1_out);
  not not_6 (not_6_out, nand_1_out);
  and and_2 (and_2_out, not_4_out, set);
  or or_2 (or_2_out, clr, set);
  and and_3 (and_3_out, not_5_out, not_2_out, d);
  and and_4 (and_4_out, not_5_out, not_2_out, not_3_out);
  not not_7 (not_7_out, or_2_out);
  nor nor_1 (nor_1_out, and_1_out, and_3_out);
  and and_5 (and_5_out, not_7_out, clk, nand_1_out);
  and and_6 (and_6_out, not_7_out, clk, not_6_out);
  d_ff_async d_ff_async_1 (.d(in_5), .clk(in_6), .set(in_7), .clr(in_8), .q(out_11), .q_bar(out_12));
  nor nor_2 (nor_2_out, clr, and_4_out);
  nor nor_3 (nor_3_out, and_2_out, and_5_out);
  nand nand_1 (nand_1_out, nor_1_out, nand_2_out);
  nor nor_4 (nor_4_out, clr, and_6_out);
  nand nand_2 (nand_2_out, nand_1_out, nor_2_out);
  nand nand_3 (q, nor_3_out, q_bar);
  nand nand_4 (q_bar, q, nor_4_out);

  // Notes on the sheet:
  //   clr_bar
  //   SET_eff
  //   ASYNC
  //   clk_bar
  //   d_bar
  //   clr_bar
  //   NORMAL
  //   SET_eff
  //   ASYNC
  //   SD
  //   RD
  //   NORMAL
  //   S_bar
  //   SD
  //   RD
  //   R_bar
  //   S_bar
  //   L
  //   R_bar
  //   L_bar
  //   L
  //   L_bar
endmodule

// VHDL entity d_ff_async, as the project stores it:
library ieee;
use ieee.std_logic_1164.all;

entity d_ff_async is
    port (
        d, clk, set, clr : in std_logic;
        q, q_bar : out std_logic
    );
end d_ff_async;

architecture rtl of d_ff_async is
    signal qi : std_logic;
begin
    process(clk, set, clr)
    begin
        if clr = '1' then
            qi <= '0';
        elsif set = '1' then
            qi <= '1';
        elsif rising_edge(clk) then
            qi <= d;
        end if;
    end process;

    q <= qi;
    q_bar <= not qi;
end rtl;
